// Logisim project TinyCPU.circ as structural Verilog: 6 circuits, main circuit TinyCPU
module TinyCPU (
  input  CLK,
  output HALTED
);

  // FetchDecode fetchdecode_1: pin names not known; wires that end beside it: CLK
  // Datapath datapath_1: pin names not known; wires that end beside it: CLK
  // AddressPath addresspath_1: pin names not known; wires that end beside it: CLK
  // Memory memory_1: pin names not known; wires that end beside it: CLK
  // ErrorFlags errorflags_1: pin names not known; wires that end beside it: CLK

  assign HALTED = CLK;

  // Notes on the sheet:
  //   TinyCPU AP 5: countdown fixture and clock-edge trace boundary
endmodule

module FetchDecode (
  input  CLK,
  input  RESET,
  input  ZERO,
  input  [11:0] PROGRAM_LIMIT,
  input  NEGATIVE,
  input  ERROR,
  output [15:0] OPERAND,
  output LOAD_CONST,
  output STORE_ADDRESS,
  output ADD_ADDRESS,
  output JUMP_NOT_ZERO,
  output PRINT,
  output HALT,
  output SET_ADDR,
  output HALT_ERROR,
  output [11:0] PC_OUT,
  output LOAD_ADDRESS,
  output LOAD_ADDRESS_REGISTER,
  output LOAD_ADDRESS_REGISTER_PLUS_OFFSET,
  output ADD_CONST,
  output ADD_ADDRESS_REGISTER,
  output ADD_ADDRESS_REGISTER_PLUS_OFFSET,
  output SUB_CONST,
  output SUB_ADDRESS,
  output SUB_ADDRESS_REGISTER,
  output SUB_ADDRESS_REGISTER_PLUS_OFFSET,
  output MUL_CONST,
  output MUL_ADDRESS,
  output MUL_ADDRESS_REGISTER,
  output MUL_ADDRESS_REGISTER_PLUS_OFFSET,
  output DIV_CONST,
  output DIV_ADDRESS,
  output DIV_ADDRESS_REGISTER,
  output DIV_ADDRESS_REGISTER_PLUS_OFFSET,
  output AND_CONST,
  output AND_ADDRESS,
  output AND_ADDRESS_REGISTER,
  output AND_ADDRESS_REGISTER_PLUS_OFFSET,
  output OR_CONST,
  output OR_ADDRESS,
  output OR_ADDRESS_REGISTER,
  output OR_ADDRESS_REGISTER_PLUS_OFFSET,
  output STORE_ADDRESS_REGISTER,
  output STORE_ADDRESS_REGISTER_PLUS_OFFSET,
  output LOAD_ADDRESS_REGISTER_CONST,
  output LOAD_ADDRESS_REGISTER_ADDRESS,
  output NOT,
  output JUMP_ADDRESS,
  output JUMP_ZERO,
  output JUMP_NEGATIVE,
  output JUMP_ERROR,
  output JUMP_NOT_ERROR,
  output CLEAR_ERROR,
  output INPUT,
  output PRINT_ADDRESS,
  output SET_OVF,
  output SET_DIV0,
  output SET_INV,
  output SET_ILL,
  output SET_INPUT
);

  wire PC_INCREMENT_p2, PC_p1, PC_SOURCE_p2;
  wire [18:16] INSTRUCTION_ROM_data;

  // Register #(.width(12)) PC: pin names not known; wires that end beside it: PC_p1, CLK, RESET
  // Adder #(.width(12)) PC_INCREMENT: pin names not known; wires that end beside it: PC_OUT, PC_INCREMENT_p2
  // Multiplexer #(.select(1), .width(12)) PC_SOURCE: pin names not known; wires that end beside it: PC_INCREMENT_p2, PC_SOURCE_p2, PC_p1
  ROM #(.addrWidth(12), .dataWidth(19)) INSTRUCTION_ROM (.addr(PC_OUT), .data({INSTRUCTION_ROM_data, OPERAND}));
  Comparator #(.width(12)) PC_RANGE (.a(PC_OUT), .b(PROGRAM_LIMIT), .eq(HALT));  // open: gt, lt
  // Decoder #(.select(6)) ISA_DECODER: pin names not known; wires that end beside it: {INSTRUCTION_ROM_data, OPERAND}, LOAD_CONST, STORE_ADDRESS, ADD_ADDRESS, JUMP_NOT_ZERO
  // AND_Gate JNZ_TAKEN has open pins: out=PC_SOURCE_p2
  // OR_Gate ERROR_HALT has open pins: out=HALT
  // Pins of 16 and 19 bits meet at {INSTRUCTION_ROM_data, OPERAND}

  assign HALT_ERROR = HALT;
  assign SET_ADDR = HALT;

  // Notes on the sheet:
  //   AP 6 symbolic ISA controls; selector values remain provisional until AP 7 defines the machine format
  //   contents of INSTRUCTION_ROM (hex, n*v repeats v):
  //   0ffff 10065 00003 10064 40000 20065 10064 30004 50000
endmodule

module Datapath (
  input  [15:0] DATA_IN,
  input  ACC_LOAD,
  input  VALID_IN,
  input  CLK,
  output [15:0] ACC_OUT,
  output ACC_VALID_OUT,
  output ZERO,
  output NEGATIVE
);

  wire undriven;

  Register #(.width(16)) ACC (.D(DATA_IN), .Q(ACC_OUT), .clk(undriven));  // open: en, clr
  Register #(.width(1)) ACC_VALID (.D(VALID_IN), .Q(ACC_VALID_OUT), .clk(undriven));  // open: en, clr
  Comparator #(.mode("twosComplement"), .width(16)) ACC_STATUS (
    .a(ACC_OUT), .b({16{1'b0}}), .eq(ZERO), .lt(NEGATIVE));  // open: gt

  // Notes on the sheet:
  //   Clocked 16-bit accumulator; signed comparator derives ZERO and NEGATIVE
endmodule

module AddressPath (
  input  [11:0] ADDRESS_IN,
  input  [11:0] OFFSET,
  input  AR_LOAD,
  input  VALID_IN,
  input  CLK,
  output [11:0] ADDRESS,
  output ADDRESS_VALID,
  output [11:0] ADDRESS_PLUS_OFFSET,
  output OFFSET_CARRY
);

  Register #(.width(12)) AR (.D(ADDRESS_IN), .Q(ADDRESS), .clk(AR_LOAD));  // open: en, clr
  Register #(.width(1)) AR_VALID (.D(VALID_IN), .Q(ADDRESS_VALID), .clk(AR_LOAD));  // open: en, clr
  // Adder #(.width(12)) OFFSET_ADDER: pin names not known; wires that end beside it: ADDRESS, OFFSET, ADDRESS_PLUS_OFFSET, OFFSET_CARRY

  // Notes on the sheet:
  //   Clocked 12-bit address register with combinational offset addition
endmodule

module Memory (
  input  [11:0] ADDRESS,
  input  [15:0] DATA_IN,
  input  VALID_IN,
  input  WRITE_ENABLE,
  input  CLK,
  output [15:0] DATA_OUT,
  output VALID_OUT
);

  wire DATA_RAM_p2, DATA_RAM_p3, DATA_RAM_p10;

  // RAM #(.addrWidth(12), .dataWidth(16)) DATA_RAM: pin names not known; wires that end beside it: DATA_IN, DATA_RAM_p2, DATA_RAM_p3, ADDRESS, VALID_IN, DATA_RAM_p2, DATA_RAM_p3, DATA_OUT, VALID_OUT, DATA_RAM_p10
  // RAM #(.addrWidth(12), .dataWidth(1)) VALID_RAM: pin names not known; wires that end beside it: VALID_IN, DATA_RAM_p2, DATA_RAM_p3, VALID_OUT, DATA_RAM_p10

  // Notes on the sheet:
  //   4096-word value/valid memory with shared address, write-enable, and clock
endmodule

module ErrorFlags (
  input  CLEAR_ERROR,
  input  CLK,
  input  SET_OVF,
  input  SET_DIV0,
  input  SET_ADDR,
  input  SET_INV,
  input  SET_ILL,
  input  SET_INPUT,
  output OVF_OUT,
  output DIV0_OUT,
  output ADDR_OUT,
  output INV_OUT,
  output ILL_OUT,
  output INPUT_OUT
);

  wire HOLD_ADDR_p2, HOLD_DIV0_p2, HOLD_ILL_p2, HOLD_INPUT_p2, HOLD_INV_p2, HOLD_OVF_p2, NEXT_ADDR_out,
       NEXT_DIV0_out, NEXT_ILL_out, NEXT_INPUT_out, NEXT_INV_out, NEXT_OVF_out, NOT_CLEAR_ERROR_out;

  not NOT_CLEAR_ERROR (NOT_CLEAR_ERROR_out, CLEAR_ERROR);
  // AND_Gate HOLD_OVF: pin names not known; wires that end beside it: NOT_CLEAR_ERROR_out, HOLD_OVF_p2
  // AND_Gate HOLD_DIV0: pin names not known; wires that end beside it: NOT_CLEAR_ERROR_out, HOLD_DIV0_p2
  // AND_Gate HOLD_ADDR: pin names not known; wires that end beside it: NOT_CLEAR_ERROR_out, HOLD_ADDR_p2
  // AND_Gate HOLD_INV: pin names not known; wires that end beside it: NOT_CLEAR_ERROR_out, HOLD_INV_p2
  // AND_Gate HOLD_ILL: pin names not known; wires that end beside it: NOT_CLEAR_ERROR_out, HOLD_ILL_p2
  // AND_Gate HOLD_INPUT: pin names not known; wires that end beside it: NOT_CLEAR_ERROR_out, HOLD_INPUT_p2
  or NEXT_OVF (NEXT_OVF_out, SET_OVF, HOLD_OVF_p2);
  or NEXT_DIV0 (NEXT_DIV0_out, SET_DIV0, HOLD_DIV0_p2);
  or NEXT_ADDR (NEXT_ADDR_out, SET_ADDR, HOLD_ADDR_p2);
  or NEXT_INV (NEXT_INV_out, SET_INV, HOLD_INV_p2);
  or NEXT_ILL (NEXT_ILL_out, SET_ILL, HOLD_ILL_p2);
  or NEXT_INPUT (NEXT_INPUT_out, SET_INPUT, HOLD_INPUT_p2);
  // Register #(.width(1)) OVF: pin names not known; wires that end beside it: NEXT_OVF_out, NEXT_DIV0_out, OVF_OUT, DIV0_OUT, NOT_CLEAR_ERROR_out, NOT_CLEAR_ERROR_out
  // Register #(.width(1)) DIV0: pin names not known; wires that end beside it: NEXT_DIV0_out, NEXT_ADDR_out, ADDR_OUT, NOT_CLEAR_ERROR_out, NOT_CLEAR_ERROR_out
  // Register #(.width(1)) ADDR: pin names not known; wires that end beside it: NEXT_ADDR_out, NEXT_INV_out, INV_OUT, NOT_CLEAR_ERROR_out, NOT_CLEAR_ERROR_out
  // Register #(.width(1)) INV: pin names not known; wires that end beside it: NEXT_INV_out, NEXT_ILL_out, ILL_OUT, NOT_CLEAR_ERROR_out, NOT_CLEAR_ERROR_out
  // Register #(.width(1)) ILL: pin names not known; wires that end beside it: NEXT_ILL_out, NEXT_INPUT_out, INPUT_OUT, NOT_CLEAR_ERROR_out, NOT_CLEAR_ERROR_out
  // Register #(.width(1)) INPUT: pin names not known; wires that end beside it: NEXT_INPUT_out, NOT_CLEAR_ERROR_out

  // Notes on the sheet:
  //   Set-dominant sticky flags: SET OR (current AND NOT CLEAR_ERROR)
endmodule
